// Digital circuit ex3.dig as structural Verilog
module ex3 (
  input  [1:0] A,
  input  [1:0] B,
  output Y
);

  wire and_1_out, and_2_out, and_3_out, nB0, nB1, xnor_1_out;

  not not_1 (nB1, B[0]);
  not not_2 (nB0, B[1]);
  and and_1 (and_1_out, A[1], nB0);
  xnor xnor_1 (xnor_1_out, A[1], B[1]);
  and and_2 (and_2_out, A[0], nB1);
  and and_3 (and_3_out, xnor_1_out, and_2_out);
  or or_1 (Y, and_1_out, and_3_out);

  // Other names for the same wires on the sheet: A1 = A[0]; A0 = A[1]; B1 = B[0]; B0 = B[1]
endmodule

/* Test case EX3 Test:
A B Y 

 0b00 0b00 0
 0b00 0b01 0
 0b00 0b10 0
 0b00 0b11 0
 0b01 0b00 1
 0b01 0b01 0
 0b01 0b10 0
 0b01 0b11 0
 0b10 0b00 1
 0b10 0b01 1
 0b10 0b10 0
 0b10 0b11 0
 0b11 0b00 1
 0b11 0b01 1
 0b11 0b10 1
 0b11 0b11 0
*/
