// Digital circuit register-file.dig as structural Verilog
module register_file (
  input  [4:0] ReadReg1,
  input  [4:0] ReadReg2,
  input  [4:0] WriteReg,
  input  [31:0] WriteData,
  input  RegWrite,
  input  Clock,
  output [31:0] ReadData1,
  output [31:0] ReadData2
);

  wire and_1_out, and_2_out, and_3_out, and_4_out, and_5_out, and_6_out, and_7_out, and_8_out, and_9_out,
       and_10_out, and_11_out, and_12_out, and_13_out, and_14_out, and_15_out, and_16_out, and_17_out,
       and_18_out, and_19_out, and_20_out, and_21_out, and_22_out, and_23_out, and_24_out, and_25_out,
       and_26_out, and_27_out, and_28_out, and_29_out, and_30_out, and_31_out, write1, write2, write3,
       write4, write5, write6, write7, write8, write9, write10, write11, write12, write13, write14, write15,
       write16, write17, write18, write19, write20, write21, write22, write23, write24, write25, write26,
       write27, write28, write29, write30, write31;
  wire [31:0] x1, x2, x3, x4, x5, x6, x7, x8, x9, x10, x11, x12, x13, x14, x15, x16, x17, x18, x19, x20, x21,
       x22, x23, x24, x25, x26, x27, x28, x29, x30, x31;

  and and_1 (and_1_out, RegWrite, write1);
  and and_2 (and_2_out, RegWrite, write2);
  and and_3 (and_3_out, RegWrite, write3);
  and and_4 (and_4_out, RegWrite, write4);
  and and_5 (and_5_out, RegWrite, write5);
  and and_6 (and_6_out, RegWrite, write6);
  and and_7 (and_7_out, RegWrite, write7);
  Register #(.Bits(32)) u_x1 (.D(WriteData), .C(Clock), .en(and_1_out), .Q(x1));
  Register #(.Bits(32)) u_x2 (.D(WriteData), .C(Clock), .en(and_2_out), .Q(x2));
  Register #(.Bits(32)) u_x3 (.D(WriteData), .C(Clock), .en(and_3_out), .Q(x3));
  Register #(.Bits(32)) u_x4 (.D(WriteData), .C(Clock), .en(and_4_out), .Q(x4));
  Register #(.Bits(32)) u_x5 (.D(WriteData), .C(Clock), .en(and_5_out), .Q(x5));
  Register #(.Bits(32)) u_x6 (.D(WriteData), .C(Clock), .en(and_6_out), .Q(x6));
  Register #(.Bits(32)) u_x7 (.D(WriteData), .C(Clock), .en(and_7_out), .Q(x7));
  and and_8 (and_8_out, RegWrite, write8);
  and and_9 (and_9_out, RegWrite, write9);
  and and_10 (and_10_out, RegWrite, write10);
  and and_11 (and_11_out, RegWrite, write11);
  and and_12 (and_12_out, RegWrite, write12);
  and and_13 (and_13_out, RegWrite, write13);
  and and_14 (and_14_out, RegWrite, write14);
  and and_15 (and_15_out, RegWrite, write15);
  Register #(.Bits(32)) u_x8 (.D(WriteData), .C(Clock), .en(and_8_out), .Q(x8));
  Register #(.Bits(32)) u_x9 (.D(WriteData), .C(Clock), .en(and_9_out), .Q(x9));
  Register #(.Bits(32)) u_x10 (.D(WriteData), .C(Clock), .en(and_10_out), .Q(x10));
  Register #(.Bits(32)) u_x11 (.D(WriteData), .C(Clock), .en(and_11_out), .Q(x11));
  Register #(.Bits(32)) u_x12 (.D(WriteData), .C(Clock), .en(and_12_out), .Q(x12));
  Register #(.Bits(32)) u_x13 (.D(WriteData), .C(Clock), .en(and_13_out), .Q(x13));
  Register #(.Bits(32)) u_x14 (.D(WriteData), .C(Clock), .en(and_14_out), .Q(x14));
  Register #(.Bits(32)) u_x15 (.D(WriteData), .C(Clock), .en(and_15_out), .Q(x15));
  Multiplexer #(.Bits(32), .Selector_Bits(5)) multiplexer_1 (
    .sel(ReadReg1), .in_0({32{1'b0}}), .in_1(x1), .in_2(x2), .in_3(x3), .in_4(x4), .in_5(x5), .in_6(x6),
    .in_7(x7), .in_8(x8), .in_9(x9), .in_10(x10), .in_11(x11), .in_12(x12), .in_13(x13), .in_14(x14),
    .in_15(x15), .in_16(x16), .in_17(x17), .in_18(x18), .in_19(x19), .in_20(x20), .in_21(x21), .in_22(x22),
    .in_23(x23), .in_24(x24), .in_25(x25), .in_26(x26), .in_27(x27), .in_28(x28), .in_29(x29), .in_30(x30),
    .in_31(x31), .out(ReadData1));
  and and_16 (and_16_out, RegWrite, write16);
  and and_17 (and_17_out, RegWrite, write17);
  and and_18 (and_18_out, RegWrite, write18);
  and and_19 (and_19_out, RegWrite, write19);
  and and_20 (and_20_out, RegWrite, write20);
  and and_21 (and_21_out, RegWrite, write21);
  and and_22 (and_22_out, RegWrite, write22);
  and and_23 (and_23_out, RegWrite, write23);
  Register #(.Bits(32)) u_x16 (.D(WriteData), .C(Clock), .en(and_16_out), .Q(x16));
  Register #(.Bits(32)) u_x17 (.D(WriteData), .C(Clock), .en(and_17_out), .Q(x17));
  Register #(.Bits(32)) u_x18 (.D(WriteData), .C(Clock), .en(and_18_out), .Q(x18));
  Register #(.Bits(32)) u_x19 (.D(WriteData), .C(Clock), .en(and_19_out), .Q(x19));
  Register #(.Bits(32)) u_x20 (.D(WriteData), .C(Clock), .en(and_20_out), .Q(x20));
  Register #(.Bits(32)) u_x21 (.D(WriteData), .C(Clock), .en(and_21_out), .Q(x21));
  Register #(.Bits(32)) u_x22 (.D(WriteData), .C(Clock), .en(and_22_out), .Q(x22));
  Register #(.Bits(32)) u_x23 (.D(WriteData), .C(Clock), .en(and_23_out), .Q(x23));
  Multiplexer #(.Selector_Bits(5), .Bits(32)) multiplexer_2 (
    .sel(ReadReg2), .in_0({32{1'b0}}), .in_1(x1), .in_2(x2), .in_3(x3), .in_4(x4), .in_5(x5), .in_6(x6),
    .in_7(x7), .in_8(x8), .in_9(x9), .in_10(x10), .in_11(x11), .in_12(x12), .in_13(x13), .in_14(x14),
    .in_15(x15), .in_16(x16), .in_17(x17), .in_18(x18), .in_19(x19), .in_20(x20), .in_21(x21), .in_22(x22),
    .in_23(x23), .in_24(x24), .in_25(x25), .in_26(x26), .in_27(x27), .in_28(x28), .in_29(x29), .in_30(x30),
    .in_31(x31), .out(ReadData2));
  and and_24 (and_24_out, RegWrite, write24);
  and and_25 (and_25_out, RegWrite, write25);
  and and_26 (and_26_out, RegWrite, write26);
  and and_27 (and_27_out, RegWrite, write27);
  and and_28 (and_28_out, RegWrite, write28);
  and and_29 (and_29_out, RegWrite, write29);
  and and_30 (and_30_out, RegWrite, write30);
  and and_31 (and_31_out, RegWrite, write31);
  Register #(.Bits(32)) u_x24 (.D(WriteData), .C(Clock), .en(and_24_out), .Q(x24));
  Register #(.Bits(32)) u_x25 (.D(WriteData), .C(Clock), .en(and_25_out), .Q(x25));
  Register #(.Bits(32)) u_x26 (.D(WriteData), .C(Clock), .en(and_26_out), .Q(x26));
  Register #(.Bits(32)) u_x27 (.D(WriteData), .C(Clock), .en(and_27_out), .Q(x27));
  Register #(.Bits(32)) u_x28 (.D(WriteData), .C(Clock), .en(and_28_out), .Q(x28));
  Register #(.Bits(32)) u_x29 (.D(WriteData), .C(Clock), .en(and_29_out), .Q(x29));
  Register #(.Bits(32)) u_x30 (.D(WriteData), .C(Clock), .en(and_30_out), .Q(x30));
  Register #(.Bits(32)) u_x31 (.D(WriteData), .C(Clock), .en(and_31_out), .Q(x31));
  Decoder #(.Selector_Bits(5)) decoder_1 (
    .sel(WriteReg), .out_1(write1), .out_2(write2), .out_3(write3), .out_4(write4), .out_5(write5),
    .out_6(write6), .out_7(write7), .out_8(write8), .out_9(write9), .out_10(write10), .out_11(write11),
    .out_12(write12), .out_13(write13), .out_14(write14), .out_15(write15), .out_16(write16),
    .out_17(write17), .out_18(write18), .out_19(write19), .out_20(write20), .out_21(write21),
    .out_22(write22), .out_23(write23), .out_24(write24), .out_25(write25), .out_26(write26),
    .out_27(write27), .out_28(write28), .out_29(write29), .out_30(write30), .out_31(write31));  // open: out_0

  // Notes on the sheet:
  //   Read Data Determination Stage
  //   Write Engage Bit Decoding Stage
endmodule

/* Test case Register File Test:
WriteReg WriteData RegWrite Clock ReadReg1 ReadReg2 ReadData1 ReadData2

# $1 = 25
1 25 1 C 1 0 25 0

# $2 = 30
2 30 1 C 0 2 0 30

# $(N+1) = (N+1)
loop(N, 30)
	(N+1) (N+1) 1 C (N+1) (N) (N+1) (N)
end loop

# $(N+1) = N-60
loop(N, 30)
	(N+1) (N-60) 1 C (N+1) (N+1) (N-60) (N-60)
end loop

# Try writing to $0. This should not write anything
0 25 1 C 0 0 0 0

# try writing when RegWrite = 0
# (the registers should still have their old values)
loop(N, 30)
	(N+1) (N+80) 0 C (N+1) (N+1) (N-60) (N-60)
end loop
*/
