// Digital circuit alu.dig as structural Verilog
module alu (
  input  [31:0] A,
  input  [31:0] B,
  input  [3:0] ALUOp,
  output FlagZ,
  output [31:0] Result
);

  wire isADD, isAND, isBoolGroup, isOR, isShiftGroup, isSLL, isSLT, isSRA, isSRL, isSUB, isXOR, or_2_out,
       or_5_out, or_6_out, Overflow, Sign, SLT1, Sub;
  wire [1:0] Bool, S;
  wire [31:0] AddSubOut, BoolOut, ShiftOut;

  Comparator #(.Bits(4)) comparator_1 (.a(ALUOp), .b(4'b0000), .eq(isAND));  // open: gt, lt
  Comparator #(.Bits(4)) comparator_2 (.a(ALUOp), .b(4'b0001), .eq(isOR));  // open: gt, lt
  Comparator #(.Bits(4)) comparator_3 (.a(ALUOp), .b(4'b0010), .eq(isADD));  // open: gt, lt
  Comparator #(.Bits(4)) comparator_4 (.a(ALUOp), .b(4'b0011), .eq(isXOR));  // open: gt, lt
  Comparator #(.Bits(4)) comparator_5 (.a(ALUOp), .b(4'b0100), .eq(isSLL));  // open: gt, lt
  Comparator #(.Bits(4)) comparator_6 (.a(ALUOp), .b(4'b0101), .eq(isSRL));  // open: gt, lt
  Comparator #(.Bits(4)) comparator_7 (.a(ALUOp), .b(4'b0110), .eq(isSUB));  // open: gt, lt
  Comparator #(.Bits(4)) comparator_8 (.a(ALUOp), .b(4'b0111), .eq(isSLT));  // open: gt, lt
  Comparator #(.Bits(4)) comparator_9 (.a(ALUOp), .b(4'b1000), .eq(isSRA));  // open: gt, lt
  or or_1 (Sub, isSUB, isSLT);
  add_sub add_sub_1 (.B(B), .A(A), .Sub(Sub), .Out(AddSubOut), .Overflow(Overflow), .Sign(Sign));
  or or_2 (or_2_out, isSRL, isXOR);
  or or_3 (Bool[0], isSRA, isOR);
  boolean_unit boolean_unit_1 (.A(A), .B(B), .Bool(Bool), .Out(BoolOut));
  // bidirectional_shifter bidirectional_shifter_1: pin names not known; wires that end beside it: A, B, Bool, ShiftOut
  or or_4 (Bool[1], or_2_out, isSRA);
  or or_5 (or_5_out, isAND, isOR);
  or or_6 (or_6_out, isSLL, isSRL);
  Comparator #(.Bits(32), .Signed("true")) comparator_10 (.a(A), .b(B), .lt(SLT1));  // open: gt, eq
  or or_7 (isBoolGroup, or_5_out, isXOR);
  or or_8 (isShiftGroup, or_6_out, isSRA);
  or or_9 (S[1], isBoolGroup, isShiftGroup);
  or or_10 (S[0], isBoolGroup, isSLT);
  Multiplexer #(.Selector_Bits(2), .Bits(32)) multiplexer_1 (
    .sel(S), .in_0(AddSubOut), .in_1({{31{1'b0}}, SLT1}), .in_2(ShiftOut), .in_3(BoolOut), .out(Result));
  Comparator #(.Bits(32)) comparator_11 (.a(Result), .b({32{1'b0}}), .eq(FlagZ));  // open: gt, lt

  // Other names for the same wires on the sheet: ALUCtrl[3:0] = ALUOp; SLT32[0] = SLT1

  // Notes on the sheet:
  //   Control Bits
  //   Computing
  //   Inputs
  //   Outputs
endmodule

/* Test case ALU lab3.1 test:
A B ALUOp Result FlagZ

# ADD tests (ALUOp = 0b0010)
0x289322C4 0x01846399 0b0010 0x2A17865D 0
0x4152A22D 0x22042121 0b0010 0x6356C34E 0
0x84893212 0x0994AD1A 0b0010 0x8E1DDF2C 0
0x90A8826C 0x112109FB 0b0010 0xA1C98C67 0
0x5210C12D 0x3D04ABBC 0b0010 0x8F156CE9 0
0x90D194B5 0xB005500E 0b0010 0x40D6E4C3 0

# SUB tests (ALUOp = 0b0110)
0x39332544 0x0435FCAD 0b0110 0x34FD2897 0
0x59286AB1 0x221FB76C 0b0110 0x3708B345 0
0xECD55935 0x248C5A4B 0b0110 0xC848FEEA 0
0x902A9525 0xE5454D48 0b0110 0xAAE547DD 0
0x8211036A 0x7B13890A 0b0110 0x06FD7A60 0
0x5FE15DBE 0x8934B9B1 0b0110 0xD6ACA40D 0

# AND tests (ALUOp = 0b0000)
0xDCD84709 0x768A5AF3 0b0000 0x54884201 0
0x3D2CD361 0xF53106EF 0b0000 0x35200261 0
0x28F56E63 0x854B7D0B 0b0000 0x00416C03 0

# OR tests (ALUOp = 0b0001)
0x9201A3DE 0x2D1A9F88 0b0001 0xBF1BBFDE 0
0xD15A7517 0xB900F275 0b0001 0xF95AF777 0
0xD81DAA93 0x0AB5E9F7 0b0001 0xDABDEBF7 0

# XOR tests (ALUCtrl = 0b0011)
0x0F9EDA3F 0x885E0A47 0b0011 0x87C0D078 0
0xCA58EED8 0x514AF1FA 0b0011 0x9B121F22 0
0xC7100004 0x3553EF1E 0b0011 0xF243EF1A 0

# SLL tests (ALUOp = 0b0100), shift B left by A[4:0]
0x20693682 0x85050A62 0b0100 0x14142988 0
0x737A6607 0x00B80C2B 0b0100 0x5C061580 0
0x0000001F 0x00000001 0b0100 0x80000000 0

# SRL tests (ALUOp = 0b0101), shift B right logically by A[4:0]
0xCB126889 0x0614E24A 0b0101 0x00030A71 0
0x02352D86 0x54891132 0b0101 0x01522444 0
0x00000001 0xF0000000 0b0101 0x78000000 0

# SLT tests (ALUOp = 0b0111), signed A < B ? 1 : 0
0x289322C4 0x01846399 0b0111 0x00000000 1
0x4152A22D 0x22042121 0b0111 0x00000000 1
0x84893212 0x0994AD1A 0b0111 0x00000001 0
0x90A8826C 0x112109FB 0b0111 0x00000001 0
0x5210C12D 0x3D04ABBC 0b0111 0x00000000 1
0x90D194B5 0xB005500E 0b0111 0x00000001 0

# SRA tests (ALUOp = 0b1000), shift B right arithmetically by A[4:0]
0x00000001 0xF0000000 0b1000 0xF8000000 0
0x3B9A2707 0xE9349ED3 0b1000 0xFFD2693D 0
0x22853218 0xD175490B 0b1000 0xFFFFFFD1 0

0x00000001 0x00000002 0b0111 0x00000001 0
*/
