// Digital circuit control-unit.dig as structural Verilog
module control_unit (
  input  [6:0] opcode,
  input  [2:0] funct3,
  input  [6:0] funct7,
  output [3:0] ALUOperation,
  output [1:0] ImmSrc,
  output ALUSrc,
  output RegWrite
);

  wire and_1_out, and_2_out, and_3_out, and_4_out, and_5_out, and_6_out, and_7_out, and_8_out,
       comparator_1_eq, comparator_2_eq, comparator_3_eq, comparator_4_eq, comparator_5_eq, comparator_6_eq,
       comparator_7_eq, comparator_8_eq, comparator_9_eq, comparator_10_eq, comparator_11_eq,
       comparator_12_eq, comparator_13_eq, comparator_14_eq, comparator_15_eq, comparator_16_eq,
       comparator_17_eq, comparator_18_eq, comparator_19_eq, comparator_20_eq, comparator_21_eq,
       comparator_22_eq, comparator_23_eq, comparator_24_eq, comparator_25_eq, comparator_26_eq,
       comparator_27_eq, comparator_28_eq, comparator_29_eq, comparator_30_eq, comparator_31_eq,
       comparator_32_eq, comparator_33_eq;
  wire [2:0] priorityencoder_1_num;

  Comparator #(.Bits(7)) comparator_1 (.a(opcode), .b(7'b0110011), .eq(comparator_1_eq));  // open: gt, lt
  Comparator #(.Bits(3)) comparator_2 (.a(funct3), .b(3'b000), .eq(comparator_2_eq));  // open: gt, lt
  Comparator #(.Bits(7)) comparator_3 (.a(funct7), .b({7{1'b0}}), .eq(comparator_3_eq));  // open: gt, lt
  Comparator #(.Bits(7)) comparator_4 (.a(opcode), .b(7'b0110011), .eq(comparator_4_eq));  // open: gt, lt
  Comparator #(.Bits(3)) comparator_5 (.a(funct3), .b(3'b000), .eq(comparator_5_eq));  // open: gt, lt
  Comparator #(.Bits(7)) comparator_6 (.a(funct7), .b(7'b0100000), .eq(comparator_6_eq));  // open: gt, lt
  Comparator #(.Bits(7)) comparator_7 (.a(opcode), .b(7'b0110011), .eq(comparator_7_eq));  // open: gt, lt
  Comparator #(.Bits(3)) comparator_8 (.a(funct3), .b(3'b111), .eq(comparator_8_eq));  // open: gt, lt
  Comparator #(.Bits(7)) comparator_9 (.a(funct7), .b({7{1'b0}}), .eq(comparator_9_eq));  // open: gt, lt
  Comparator #(.Bits(7)) comparator_10 (.a(opcode), .b(7'b0110011), .eq(comparator_10_eq));  // open: gt, lt
  Comparator #(.Bits(3)) comparator_11 (.a(funct3), .b(3'b110), .eq(comparator_11_eq));  // open: gt, lt
  Comparator #(.Bits(7)) comparator_12 (.a(funct7), .b({7{1'b0}}), .eq(comparator_12_eq));  // open: gt, lt
  Comparator #(.Bits(7)) comparator_13 (.a(opcode), .b(7'b0110011), .eq(comparator_13_eq));  // open: gt, lt
  Comparator #(.Bits(3)) comparator_14 (.a(funct3), .b(3'b010), .eq(comparator_14_eq));  // open: gt, lt
  Comparator #(.Bits(7)) comparator_15 (.a(funct7), .b({7{1'b0}}), .eq(comparator_15_eq));  // open: gt, lt
  Comparator #(.Bits(7)) comparator_16 (.a(opcode), .b(7'b0010011), .eq(comparator_16_eq));  // open: gt, lt
  Comparator #(.Bits(3)) comparator_17 (.a(funct3), .b(3'b000), .eq(comparator_17_eq));  // open: gt, lt
  Comparator #(.Bits(7)) comparator_18 (.a(opcode), .b(7'b0010011), .eq(comparator_18_eq));  // open: gt, lt
  Comparator #(.Bits(3)) comparator_19 (.a(funct3), .b(3'b010), .eq(comparator_19_eq));  // open: gt, lt
  Comparator #(.Bits(7)) comparator_20 (.a(opcode), .b(7'b0010011), .eq(comparator_20_eq));  // open: gt, lt
  Comparator #(.Bits(3)) comparator_21 (.a(funct3), .b(3'b111), .eq(comparator_21_eq));  // open: gt, lt
  Comparator #(.Bits(7)) comparator_22 (.a(opcode), .b(7'b0110011), .eq(comparator_22_eq));  // open: gt, lt
  Comparator #(.Bits(3)) comparator_23 (.a(funct3), .b(3'b001), .eq(comparator_23_eq));  // open: gt, lt
  Comparator #(.Bits(7)) comparator_24 (.a(funct7), .b({7{1'b0}}), .eq(comparator_24_eq));  // open: gt, lt
  Comparator #(.Bits(7)) comparator_25 (.a(opcode), .b(7'b0110011), .eq(comparator_25_eq));  // open: gt, lt
  Comparator #(.Bits(3)) comparator_26 (.a(funct3), .b(3'b001), .eq(comparator_26_eq));  // open: gt, lt
  Comparator #(.Bits(7)) comparator_27 (.a(funct7), .b({7{1'b0}}), .eq(comparator_27_eq));  // open: gt, lt
  Comparator #(.Bits(7)) comparator_28 (.a(opcode), .b(7'b0110011), .eq(comparator_28_eq));  // open: gt, lt
  Comparator #(.Bits(3)) comparator_29 (.a(funct3), .b(3'b101), .eq(comparator_29_eq));  // open: gt, lt
  Comparator #(.Bits(7)) comparator_30 (.a(funct7), .b({7{1'b0}}), .eq(comparator_30_eq));  // open: gt, lt
  Comparator #(.Bits(7)) comparator_31 (.a(opcode), .b(7'b0110011), .eq(comparator_31_eq));  // open: gt, lt
  Comparator #(.Bits(3)) comparator_32 (.a(funct3), .b(3'b101), .eq(comparator_32_eq));  // open: gt, lt
  Comparator #(.Bits(7)) comparator_33 (.a(funct7), .b(7'b0100000), .eq(comparator_33_eq));  // open: gt, lt
  and and_1 (and_1_out, comparator_1_eq, comparator_2_eq, comparator_3_eq);
  and and_2 (and_2_out, comparator_4_eq, comparator_5_eq, comparator_6_eq);
  and and_3 (and_3_out, comparator_7_eq, comparator_8_eq, comparator_9_eq);
  and and_4 (and_4_out, comparator_10_eq, comparator_11_eq, comparator_12_eq);
  and and_5 (and_5_out, comparator_13_eq, comparator_14_eq, comparator_15_eq);
  and and_6 (and_6_out, comparator_16_eq, comparator_17_eq);
  and and_7 (and_7_out, comparator_18_eq, comparator_19_eq);
  and and_8 (and_8_out, comparator_20_eq, comparator_21_eq);
  // And and_9 has open pins: In_1=comparator_22_eq, In_2=comparator_23_eq, In_3=comparator_24_eq, out=open
  // And and_10 has open pins: In_1=comparator_25_eq, In_2=comparator_26_eq, In_3=comparator_27_eq, out=open
  // And and_11 has open pins: In_1=comparator_28_eq, In_2=comparator_29_eq, In_3=comparator_30_eq, out=open
  // And and_12 has open pins: In_1=comparator_31_eq, In_2=comparator_32_eq, In_3=comparator_33_eq, out=open
  PriorityEncoder #(.Selector_Bits(3)) priorityencoder_1 (
    .in0(and_1_out), .in1(and_2_out), .in2(and_3_out), .in3(and_4_out), .in4(and_5_out), .in5(and_6_out),
    .in6(and_7_out), .in7(and_8_out), .num(priorityencoder_1_num));  // open: any
  ROM #(.AddrBits(3), .Bits(8)) rom_1 (
    .A(priorityencoder_1_num), .sel(1'b1), .D({RegWrite, ALUSrc, ImmSrc, ALUOperation}));

  // Other names for the same wires on the sheet: f3[2:0] = funct3; f7[6:0] = funct7; oc[6:0] = opcode

  // Notes on the sheet:
  //   contents of rom_1 (hex, n*v repeats v):
  //   82,86,80,81,87,c2,c7,c0
endmodule

/* Test case:
opcode funct3 funct7 ALUSrc ALUOperation
0x33   0      0x00   0      2     
0x33   0      0x20   0      6     
0x33   7      0x00   0      0     
0x33   6      0x00   0      1     
0x33   2      0x00   0      7     
0x13   0      0x00   1      2     
0x13   7      0x00   1      0     
0x13   2      0x00   1      7
0x13   2      0x7F   1      7
*/
