// Digital circuit cpu.dig as structural Verilog
module cpu (
  input  clk,
  output [31:0] ReadData1,
  output [31:0] ReadData2
);

  wire ALUSrc, RegWrite;
  wire [2:0] f3;
  wire [3:0] ALUOp;
  wire [4:0] i, r1, rd;
  wire [6:0] f7, oc;
  wire [31:0] add_1_s, bitextender_1_out, multiplexer_1_out, PC_q, WriteData;

  control_unit control_unit_1 (
    .opcode(oc), .funct3(f3), .funct7(f7), .ALUOperation(ALUOp), .ALUSrc(ALUSrc), .RegWrite(RegWrite));  // open: ImmSrc
  register_file register_file_1 (
    .ReadReg1(r1), .ReadReg2(i), .WriteReg(rd), .WriteData(WriteData), .RegWrite(RegWrite), .Clock(clk),
    .ReadData1(ReadData1), .ReadData2(ReadData2));
  Register #(.Bits(32), .isProgramCounter("true")) PC (.D(add_1_s), .C(clk), .en(1'b1), .Q(PC_q));
  BitExtender #(.inputBits(12), .outputBits(32)) bitextender_1 (.in({f7, i}), .out(bitextender_1_out));
  Add #(.Bits(32)) add_1 (.a(32'h4), .b(PC_q), .c_i(1'b0), .s(add_1_s));  // open: c_o
  Multiplexer #(.Bits(32)) multiplexer_1 (
    .sel(ALUSrc), .in_0(ReadData2), .in_1(bitextender_1_out), .out(multiplexer_1_out));
  ROM #(.AddrBits(10), .isProgramMemory("true"), .Bits(32)) Instruction_Memory (
    .A(PC_q[11:2]), .sel(1'b1), .D({f7, i, r1, f3, rd, oc}));
  alu alu_1 (.A(ReadData1), .B(multiplexer_1_out), .ALUOp(ALUOp), .Result(WriteData));  // open: FlagZ

  // Other names for the same wires on the sheet: r2[4:0] = i; i[11:5] = f7; clock = clk

  // Notes on the sheet:
  //   contents of Instruction_Memory (hex, n*v repeats v):
  //   fec00213,7f020293,70128313,53130393,12337713,71c77793,5417f893
  //   ,13722913,292993,9aa13,ffda2a93,5aab13,b0013,fec22b93,b8013,fa65ac13
  //   ,c0013,22c93,c8013,2585ad13,d0013,fff22d93,d8013
endmodule

/* Test case cpu:
clk ReadData1 ReadData2
0 0 0        # addi x4, x0, -20
C (-20) 0    # addi x5, x4, 0x7F0      ; x4 = -20
C 2012 0     # addi x6, x5, 0x701      ; x5 = 2012
C 3805 0     # addi x7, x6, 0x531      ; x6 = 3805
C 3805 0     # andi x14, x6, 0x123     ; rs1 = x6
C 1 0        # andi x15, x14, 0x71C    ; rs1 = x14 = 1
C 0 0        # andi x17, x15, 0x541    ; rs1 = x15 = 0
C (-20) 0    # slti x18, x4, 311       ; rs1 = x4
C 1 0        # slti x19, x18, 2        ; rs1 = x18 = 1
C 1 0        # slti x20, x19, 0        ; rs1 = x19 = 1
C 0 0        # slti x21, x20, -3       ; rs1 = x20 = 0
C 0 2012     # slti x22, x21, 5        ; rs1 = x21 = 0
C 1 0        # addi x0,  x22, 0        ; rs1 = x22 = 1 
C (-20) 0    # slti x23, x4,  -20      ; rs1 = x4
C 0 0        # addi x0,  x23, 0        ; rs1 = x23 = 0
C 0 3805     # slti x24, x11, -90      ; x11 was never set, so 0
C 0 0        # addi x0,  x24, 0        ; rs1 = x24 = 0
C (-20) 0    # slti x25, x4,  0        ; rs1 = x4
C 1 0        # addi x0,  x25, 0        ; rs1 = x25 = 1
C 0 0        # slti x26, x11, 600      ; x11 still 0
C 1 0        # addi x0,  x26, 0        ; rs1 = x26 = 1
C (-20) 0    # slti x27, x4,  -1       ; rs1 = x4
C 1 0        # addi x0,  x27, 0        ; rs1 = x27 = 1
*/
