// Digital circuit register-file.dig as structural Verilog
module register_file (
  input  [4:0] ReadReg1,
  input  [4:0] ReadReg2,
  input  [4:0] WriteReg,
  input  [31:0] WriteData,
  input  RegWrite,
  input  Clock,
  output [31:0] ReadData1,
  output [31:0] ReadData2
);

  wire Clock_t, En1, En2, En3, En4, En5, En6, En7, En8, En9, En10, En11, En12, En13, En14, En15, En16, En17,
       En18, En19, En20, En21, En22, En23, En24, En25, En26, En27, En28, En29, En30, En31;
  wire [31:0] Out1, Out2, Out3, Out4, Out5, Out6, Out7, Out8, Out9, Out10, Out11, Out12, Out13, Out14, Out15,
       Out16, Out17, Out18, Out19, Out20, Out21, Out22, Out23, Out24, Out25, Out26, Out27, Out28, Out29,
       Out30, Out31;

  and and_1 (Clock_t, RegWrite, Clock);
  Register #(.Bits(32)) Reg1 (.D(WriteData), .C(Clock_t), .en(En1), .Q(Out1));
  Register #(.Bits(32)) Reg2 (.D(WriteData), .C(Clock_t), .en(En2), .Q(Out2));
  Register #(.Bits(32)) Reg3 (.D(WriteData), .C(Clock_t), .en(En3), .Q(Out3));
  Register #(.Bits(32)) Reg4 (.D(WriteData), .C(Clock_t), .en(En4), .Q(Out4));
  Register #(.Bits(32)) Reg5 (.D(WriteData), .C(Clock_t), .en(En5), .Q(Out5));
  Register #(.Bits(32)) Reg6 (.D(WriteData), .C(Clock_t), .en(En6), .Q(Out6));
  Register #(.Bits(32)) Reg7 (.D(WriteData), .C(Clock_t), .en(En7), .Q(Out7));
  Register #(.Bits(32)) Reg8 (.D(WriteData), .C(Clock_t), .en(En8), .Q(Out8));
  Register #(.Bits(32)) Reg9 (.D(WriteData), .C(Clock_t), .en(En9), .Q(Out9));
  Register #(.Bits(32)) Reg10 (.D(WriteData), .C(Clock_t), .en(En10), .Q(Out10));
  Register #(.Bits(32)) Reg11 (.D(WriteData), .C(Clock_t), .en(En11), .Q(Out11));
  Register #(.Bits(32)) Reg12 (.D(WriteData), .C(Clock_t), .en(En12), .Q(Out12));
  Register #(.Bits(32)) Reg13 (.D(WriteData), .C(Clock_t), .en(En13), .Q(Out13));
  Register #(.Bits(32)) Reg14 (.D(WriteData), .C(Clock_t), .en(En14), .Q(Out14));
  Register #(.Bits(32)) Reg15 (.D(WriteData), .C(Clock_t), .en(En15), .Q(Out15));
  Register #(.Bits(32)) Reg16 (.D(WriteData), .C(Clock_t), .en(En16), .Q(Out16));
  Register #(.Bits(32)) Reg17 (.D(WriteData), .C(Clock_t), .en(En17), .Q(Out17));
  Register #(.Bits(32)) Reg18 (.D(WriteData), .C(Clock_t), .en(En18), .Q(Out18));
  Register #(.Bits(32)) Reg19 (.D(WriteData), .C(Clock_t), .en(En19), .Q(Out19));
  Register #(.Bits(32)) Reg20 (.D(WriteData), .C(Clock_t), .en(En20), .Q(Out20));
  Register #(.Bits(32)) Reg21 (.D(WriteData), .C(Clock_t), .en(En21), .Q(Out21));
  Register #(.Bits(32)) Reg22 (.D(WriteData), .C(Clock_t), .en(En22), .Q(Out22));
  Register #(.Bits(32)) Reg23 (.D(WriteData), .C(Clock_t), .en(En23), .Q(Out23));
  Register #(.Bits(32)) Reg24 (.D(WriteData), .C(Clock_t), .en(En24), .Q(Out24));
  Register #(.Bits(32)) Reg25 (.D(WriteData), .C(Clock_t), .en(En25), .Q(Out25));
  Register #(.Bits(32)) Reg26 (.D(WriteData), .C(Clock_t), .en(En26), .Q(Out26));
  Register #(.Bits(32)) Reg27 (.D(WriteData), .C(Clock_t), .en(En27), .Q(Out27));
  Register #(.Bits(32)) Reg28 (.D(WriteData), .C(Clock_t), .en(En28), .Q(Out28));
  Register #(.Bits(32)) Reg29 (.D(WriteData), .C(Clock_t), .en(En29), .Q(Out29));
  Register #(.Bits(32)) Reg30 (.D(WriteData), .C(Clock_t), .en(En30), .Q(Out30));
  Register #(.Bits(32)) Reg31 (.D(WriteData), .C(Clock_t), .en(En31), .Q(Out31));
  Multiplexer #(.Selector_Bits(5), .Bits(32)) multiplexer_1 (
    .sel(ReadReg1), .in_0({32{1'b0}}), .in_1(Out1), .in_2(Out2), .in_3(Out3), .in_4(Out4), .in_5(Out5),
    .in_6(Out6), .in_7(Out7), .in_8(Out8), .in_9(Out9), .in_10(Out10), .in_11(Out11), .in_12(Out12),
    .in_13(Out13), .in_14(Out14), .in_15(Out15), .in_16(Out16), .in_17(Out17), .in_18(Out18), .in_19(Out19),
    .in_20(Out20), .in_21(Out21), .in_22(Out22), .in_23(Out23), .in_24(Out24), .in_25(Out25), .in_26(Out26),
    .in_27(Out27), .in_28(Out28), .in_29(Out29), .in_30(Out30), .in_31(Out31), .out(ReadData1));
  Decoder #(.Selector_Bits(5)) decoder_1 (
    .sel(WriteReg), .out_1(En1), .out_2(En2), .out_3(En3), .out_4(En4), .out_5(En5), .out_6(En6),
    .out_7(En7), .out_8(En8), .out_9(En9), .out_10(En10), .out_11(En11), .out_12(En12), .out_13(En13),
    .out_14(En14), .out_15(En15), .out_16(En16), .out_17(En17), .out_18(En18), .out_19(En19), .out_20(En20),
    .out_21(En21), .out_22(En22), .out_23(En23), .out_24(En24), .out_25(En25), .out_26(En26), .out_27(En27),
    .out_28(En28), .out_29(En29), .out_30(En30), .out_31(En31));  // open: out_0
  Multiplexer #(.Selector_Bits(5), .Bits(32)) multiplexer_2 (
    .sel(ReadReg2), .in_0({32{1'b0}}), .in_1(Out1), .in_2(Out2), .in_3(Out3), .in_4(Out4), .in_5(Out5),
    .in_6(Out6), .in_7(Out7), .in_8(Out8), .in_9(Out9), .in_10(Out10), .in_11(Out11), .in_12(Out12),
    .in_13(Out13), .in_14(Out14), .in_15(Out15), .in_16(Out16), .in_17(Out17), .in_18(Out18), .in_19(Out19),
    .in_20(Out20), .in_21(Out21), .in_22(Out22), .in_23(Out23), .in_24(Out24), .in_25(Out25), .in_26(Out26),
    .in_27(Out27), .in_28(Out28), .in_29(Out29), .in_30(Out30), .in_31(Out31), .out(ReadData2));

  // Other names for the same wires on the sheet: C = Clock
endmodule

/* Test case Register File Test:
WriteReg WriteData RegWrite Clock ReadReg1 ReadReg2 ReadData1 ReadData2

# $1 = 25
1 25 1 C 1 0 25 0

# $2 = 30
2 30 1 C 0 2 0 30

# $(N+1) = (N+1)
loop(N, 30)
	(N+1) (N+1) 1 C (N+1) (N) (N+1) (N)
end loop

# $(N+1) = N-60
loop(N, 30)
	(N+1) (N-60) 1 C (N+1) (N+1) (N-60) (N-60)
end loop

# Try writing to $0. This should not write anything
0 25 1 C 0 0 0 0

# try writing when RegWrite = 0
# (the registers should still have their old values)
loop(N, 30)
	(N+1) (N+80) 0 C (N+1) (N+1) (N-60) (N-60)
end loop
*/
